# Fritzing sketch Kaffee (saved by Fritzing 0.9.3b)
breadboards: 1

parts:
  LCD1 = LCD screen
  Raspberry_Pi_1 = Raspberry Pi 3 [part_number=RPI-3-V1.2]
  Bauteil1 = RFID-RC522-v2
  LED1 = RGB LED - (4 legs) [package="5 mm [THT]"]
  S1 = Pushbutton [package="[THT]"]
  S2 = Pushbutton [package="[THT]"]
  S3 = Pushbutton [package="[THT]"]
  S4 = Pushbutton [package="[THT]"]
  R1 = Trimmer Potentiometer [maximum_resistance=10kΩ package=THT]
  R2 = Trimmer Potentiometer [maximum_resistance=10kΩ package=THT]
  IC1 = ULN2803A [package=THT]
  R6 = Resistor [tolerance=±5% resistance=90 package=THT]
  R7 = Resistor [tolerance=±5% resistance=100 package=THT]
  R8 = Resistor [tolerance=±5% resistance=10k package=THT]
  R9 = Resistor [tolerance=±5% resistance=10k package=THT]
  R10 = Resistor [tolerance=±1% resistance=10k package=THT]
  R11 = Resistor [tolerance=±5% resistance=10k package=THT]
  R12 = Resistor [tolerance=±5% resistance=10k package=THT]
  R13 = Resistor [tolerance=±5% resistance=10k package=THT]
  U1 = RELAY [package=relay-jzc]
  U2 = RELAY [package=relay-jzc]
  U3 = RELAY [package=relay-jzc]
  R5 = Resistor [tolerance=±5% resistance=150 package=THT]
  R4 = Resistor [tolerance=±5% resistance=10k package=THT]
  R3 = Resistor [tolerance=±20% resistance=10k package=THT]  # not connected

nets (from the schematic view):
  GND: LCD1.VSS, LCD1.R/W, Raspberry_Pi_1.GND, Bauteil1.GND, R2.wiper, U1.NO, U2.NO
  VDD: LCD1.VDD, Raspberry_Pi_1.5V, LED1.common_anode, R1.wiper, IC1.COM_-_Common, R8.Pin_1, R9.Pin_1, R10.Pin_1, R11.Pin_1, R12.Pin_1, R13.Pin_1, U3.COIL1
  N1: LCD1.V0, R2.leg2
  N2: LCD1.RS, Raspberry_Pi_1.GPIO4
  N3: LCD1.E, Raspberry_Pi_1.GPIO17
  N4: LCD1.DB4, Raspberry_Pi_1.GPIO18
  N5: LCD1.DB5, Raspberry_Pi_1.GPIO22
  N6: LCD1.DB6, Raspberry_Pi_1.GPIO23
  N7: LCD1.DB7, Raspberry_Pi_1.GPIO24
  N8: LCD1.LED+, R1.leg2
  N9: LCD1.LED-, IC1.Out_4
  3V3: Raspberry_Pi_1.3v3, Raspberry_Pi_1.3V3, Bauteil1.3.3V
  N10: Raspberry_Pi_1.GPIO27, IC1.In_4
  N11: Raspberry_Pi_1.GPIO10, Bauteil1.MOSI
  N12: Raspberry_Pi_1.GPIO9, Bauteil1.MISO
  N13: Raspberry_Pi_1.GPIO11, Bauteil1.SCK
  N14: Raspberry_Pi_1.GPIO6, IC1.In_5
  N15: Raspberry_Pi_1.GPIO13, IC1.In_1
  N16: Raspberry_Pi_1.GPIO19, IC1.In_2
  N17: Raspberry_Pi_1.GPIO26, IC1.In_3
  N18: Raspberry_Pi_1.GPIO21, S4.Pin_1, S4.Pin_2, R8.Pin_0
  N19: Raspberry_Pi_1.GPIO20, S3.Pin_1, S3.Pin_2, R9.Pin_0
  N20: Raspberry_Pi_1.GPIO16, S2.Pin_1, S2.Pin_2, R10.Pin_0
  N21: Raspberry_Pi_1.GPIO12, S1.Pin_1, S1.Pin_2, R11.Pin_0
  N22: Raspberry_Pi_1.GPIO8, Bauteil1.SDA
  N23: Raspberry_Pi_1.GPIO25, Bauteil1.RST
  N24: LED1.red_cathode, R5.Pin_1
  N25: S1.Pin_3, S1.Pin_4
  N26: S2.Pin_3, S2.Pin_4
  N27: S3.Pin_3, S3.Pin_4
  N28: S4.Pin_3, S4.Pin_4
  N29: IC1.Out_5, U3.COIL2
  N30: IC1.Out_3, R7.Pin_0
  N31: IC1.Out_2, R6.Pin_0
  N32: IC1.Out_1, R5.Pin_0
  N33: R12.Pin_0, U1.MAIN
  N34: R13.Pin_0, U2.MAIN
  N35: U3.NO, R4.Pin_0

custom parts:
  RFID-RC522-v2: A simple China made RFID-RC522 Reader; do check the pin labels, as this is a MFRC522 based clone.
