# Fritzing sketch KaffeeV2 (saved by Fritzing 0.9.3b)
breadboards: 1

parts:
  LCD2 = LCD screen
  R1 = Resistor [tolerance=±5% resistance=10k package=THT]
  R2 = Resistor [tolerance=±5% resistance=10k package=THT]
  R3 = Resistor [tolerance=±5% resistance=10k package=THT]
  R4 = Resistor [tolerance=±5% resistance=10k package=THT]
  R5 = Resistor [tolerance=±5% resistance=10k package=THT]
  R6 = Resistor [tolerance=±5% resistance=10k package=THT]
  S1_-_Minus = Square Pushbutton
  S2_-_Plus = Square Pushbutton
  S3_-_OK = Square Pushbutton
  S4_-_Menü = Square Pushbutton
  U1_-_Wasserpumpe = RELAY [package=relay-g5q]
  U2_-_Mahlwerk = RELAY [package=relay-g5q]
  Raspberry_Pi = Raspberry Pi B+
  IC1 = ULN2803A [package=THT]
  R7 = Trimmer Potentiometer [maximum_resistance=10kΩ package=THT]
  R8 = Trimmer Potentiometer [maximum_resistance=10kΩ package=THT]
  R9 = Resistor [tolerance=±5% resistance=150 package=THT]
  R10 = Resistor [tolerance=±5% resistance=220 package=THT]
  R11 = Resistor [tolerance=±5% resistance=100 package=THT]
  LED2 = RGB LED - (4 legs) [package="5 mm [THT]"]
  U3_-_Freigabe = RELAY [package=relay-g5q]
  R12 = Resistor [tolerance=±5% resistance=10k package=THT]
  R13 = Resistor [tolerance=±5% resistance=10k package=THT]
  Bauteil1 = RFID-RC522-v2

nets:
  GND: LCD2.VSS, LCD2.R/W, S4_-_Menü.leg0, Raspberry_Pi.39_-_GND, Raspberry_Pi.34_-_GND, Raspberry_Pi.20_-_GND, Raspberry_Pi.6_-_GND, IC1.0V, R8.leg1, Bauteil1.GND
  5V: LCD2.VDD, Raspberry_Pi.4_-_5V, Raspberry_Pi.2_-_5V, IC1.COM_-_Common, R7.leg1, LED2.common_anode, U3_-_Freigabe.COIL1
  N1: LCD2.V0, R8.wiper
  N2: LCD2.RS, Raspberry_Pi.7_-_BCM_4
  N3: LCD2.E, Raspberry_Pi.11_-_BCM_17
  N4: LCD2.DB4, Raspberry_Pi.12_-_BCM_18
  N5: LCD2.DB5, Raspberry_Pi.15_-_BCM_22
  N6: LCD2.DB6, Raspberry_Pi.16_-_BCM_23
  N7: LCD2.DB7, Raspberry_Pi.18_-_BCM_24
  N8: LCD2.LED+, R7.wiper
  N9: LCD2.LED-, IC1.Out_4
  3.3V: R1.Pin_0, R2.Pin_0, R3.Pin_0, R4.Pin_0, R5.Pin_0, R6.Pin_0, Raspberry_Pi.3v3, Raspberry_Pi.17_-_3V3, Bauteil1.3.3V
  N10: R1.Pin_1, S1_-_Minus.leg1, Raspberry_Pi.32_-_BCM_12
  N11: R2.Pin_1, S2_-_Plus.leg1, Raspberry_Pi.36_-_BCM_16
  N12: R3.Pin_1, S3_-_OK.leg1, Raspberry_Pi.40_-_BCM_21
  N13: R4.Pin_1, S4_-_Menü.leg1, Raspberry_Pi.38_-_BCM_20
  N14: R5.Pin_1, U1_-_Wasserpumpe.NO, Raspberry_Pi.29_-_BCM_5
  N15: R6.Pin_1, U2_-_Mahlwerk.NO, Raspberry_Pi.26_-_BCM_7
  N16: S1_-_Minus.leg0, S2_-_Plus.leg0, S3_-_OK.leg0, U1_-_Wasserpumpe.MAIN, U2_-_Mahlwerk.MAIN
  N17: Raspberry_Pi.13_-_BCM_27, IC1.In_4
  N18: Raspberry_Pi.19_-_BCM_10, Bauteil1.MOSI
  N19: Raspberry_Pi.21_-_BCM_9, Bauteil1.MISO
  N20: Raspberry_Pi.23_-_BCM_11, Bauteil1.SCK
  N21: Raspberry_Pi.31_-_BCM_6, IC1.In_5
  N22: Raspberry_Pi.33_-_BCM_13, IC1.In_1
  N23: Raspberry_Pi.35_-_BCM_19, IC1.In_2
  N24: Raspberry_Pi.37_-_BCM_26, IC1.In_3
  N25: Raspberry_Pi.24_-_BCM_8, Bauteil1.SDA
  N26: Raspberry_Pi.22_-_BCM_25, Bauteil1.RST
  N27: IC1.Out_5, U3_-_Freigabe.COIL2
  N28: IC1.Out_3, R10.Pin_1
  N29: IC1.Out_2, R11.Pin_1
  N30: IC1.Out_1, R9.Pin_1
  N31: R9.Pin_0, LED2.red_cathode
  N32: R10.Pin_0, LED2.blue_cathode
  N33: R11.Pin_0, LED2.green_cathode
  N34: U3_-_Freigabe.NO, R12.Pin_0, R13.Pin_0

notes:
  Hier Ader von Kaffeetasterplatine
  Hier Adern zur Kaffeetasterplatine
  Spulen werden von Kaffee MA angesteuert
  ACHTUNG Darstellungsproblem: RST ist nicht mit GND verbunden, GND = GND - RST auf PI

custom parts:
  Raspberry Pi B+: Eigene Beschriftung
  RFID-RC522-v2: A simple China made RFID-RC522 Reader; do check the pin labels, as this is a MFRC522 based clone.
