# Fritzing sketch KaffeeV2 (saved by Fritzing 0.9.3b)
breadboards: 1

parts:
  LCD1 = LCD screen
  R1 = Resistor [tolerance=±5% resistance=10k package=THT]
  R2 = Resistor [tolerance=±5% resistance=10k package=THT]
  R3 = Resistor [tolerance=±5% resistance=10k package=THT]
  R4 = Resistor [tolerance=±5% resistance=10k package=THT]
  R5 = Resistor [tolerance=±5% resistance=10k package=THT]
  R6 = Resistor [tolerance=±5% resistance=10k package=THT]
  S1_-_Minus = Square Pushbutton
  S2_-_Plus = Square Pushbutton
  S3_-_OK = Square Pushbutton
  S4_-_Menü = Square Pushbutton
  U1_-_Wasserpumpe = RELAY [package=relay-g5q]
  U2_-_Mahlwerk = RELAY [package=relay-g5q]
  Raspberry_Pi = Raspberry Pi B+
  IC1 = ULN2803A [package=THT]
  R9 = Resistor [tolerance=±5% resistance=150 package=THT]
  R10 = Resistor [tolerance=±5% resistance=220 package=THT]
  R11 = Resistor [tolerance=±5% resistance=100 package=THT]
  LED2 = RGB LED - (4 legs) [package="5 mm [THT]"]
  U3_-_Freigabe = RELAY [package=relay-g5q]
  R12 = Resistor [tolerance=±5% resistance=10k package=THT]
  R13 = Resistor [tolerance=±5% resistance=10k package=THT]
  Bauteil1 = RFID-RC522-v2
  Bauteil2 = Logic Level Converter
  U1 = PCF8574 [package="DIP16 [THT]"]
  C1 = Ceramic Capacitor [capacitance=100nF package="100 mil [THT, multilayer]"]
  C2 = Ceramic Capacitor [capacitance=100nF package="100 mil [THT, multilayer]"]
  C3 = Ceramic Capacitor [capacitance=100nF package="100 mil [THT, multilayer]"]
  C4 = Ceramic Capacitor [capacitance=100nF package="100 mil [THT, multilayer]"]
  C5 = Ceramic Capacitor [capacitance=100nF package="100 mil [THT, multilayer]"]
  C6 = Ceramic Capacitor [capacitance=100nF package="100 mil [THT, multilayer]"]

nets:
  GND: LCD1.VSS, S4_-_Menü.leg0, Raspberry_Pi.34_-_GND, Raspberry_Pi.30_-_GND, Raspberry_Pi.6_-_GND, IC1.0V, Bauteil1.GND, Bauteil2.GND, U1.GND, C4.0
  5V: LCD1.VDD, Raspberry_Pi.4_-_5V, Raspberry_Pi.2_-_5V, IC1.COM_-_Common, LED2.common_anode, U3_-_Freigabe.COIL1, Bauteil2.HV, U1.VCC
  3.3V: R1.Pin_0, R2.Pin_0, R3.Pin_0, R4.Pin_0, R5.Pin_0, R6.Pin_0, Raspberry_Pi.3v3, Raspberry_Pi.17_-_3V3, Bauteil1.3.3V, Bauteil2.LV
  N1: R1.Pin_1, S1_-_Minus.leg1, Raspberry_Pi.32_-_BCM_12, C1.1
  N2: R2.Pin_1, S2_-_Plus.leg1, Raspberry_Pi.36_-_BCM_16, C2.1
  N3: R3.Pin_1, S3_-_OK.leg1, Raspberry_Pi.40_-_BCM_21, C3.1
  N4: R4.Pin_1, S4_-_Menü.leg1, Raspberry_Pi.38_-_BCM_20, C4.1
  N5: R5.Pin_1, U1_-_Wasserpumpe.NO, Raspberry_Pi.29_-_BCM_5, C5.0
  N6: R6.Pin_1, U2_-_Mahlwerk.NO, Raspberry_Pi.26_-_BCM_7, C6.0
  N7: S1_-_Minus.leg0, S2_-_Plus.leg0, S3_-_OK.leg0, U1_-_Wasserpumpe.MAIN, U2_-_Mahlwerk.MAIN, C1.0, C2.0, C3.0, C5.1, C6.1
  N8: Raspberry_Pi.3_-_BCM_2, Bauteil2.TX2_LV
  N9: Raspberry_Pi.5_-_BCM_3, Bauteil2.TX_LV
  N10: Raspberry_Pi.13_-_BCM_27, IC1.In_4
  N11: Raspberry_Pi.19_-_BCM_10, Bauteil1.MOSI
  N12: Raspberry_Pi.21_-_BCM_9, Bauteil1.MISO
  N13: Raspberry_Pi.23_-_BCM_11, Bauteil1.SCK
  N14: Raspberry_Pi.31_-_BCM_6, IC1.In_5
  N15: Raspberry_Pi.33_-_BCM_13, IC1.In_1
  N16: Raspberry_Pi.35_-_BCM_19, IC1.In_2
  N17: Raspberry_Pi.37_-_BCM_26, IC1.In_3
  N18: Raspberry_Pi.24_-_BCM_8, Bauteil1.SDA
  N19: Raspberry_Pi.22_-_BCM_25, Bauteil1.RST
  N20: IC1.Out_5, U3_-_Freigabe.COIL2
  N21: IC1.Out_3, R10.Pin_1
  N22: IC1.Out_2, R11.Pin_1
  N23: IC1.Out_1, R9.Pin_1
  N24: R9.Pin_0, LED2.red_cathode
  N25: R10.Pin_0, LED2.blue_cathode
  N26: R11.Pin_0, LED2.green_cathode
  N27: U3_-_Freigabe.NO, R12.Pin_0, R13.Pin_0
  N28: Bauteil2.TX_HV, U1.SCL
  N29: Bauteil2.TX2_HV, U1.SDA

notes:
  Hier Ader von Kaffeetasterplatine
  Hier Adern zur Kaffeetasterplatine
  Spulen werden von Kaffee MA angesteuert
  ACHTUNG Darstellungsproblem: RST ist nicht mit GND verbunden, GND = GND - RST auf PI
  der rest ist zwischen display und i2c baustein verbunden
  Ersatzbild für allg. Level Shifter
  Kondensatoren so nah wie möglich beim GPIO Eingang verlöten

custom parts:
  Raspberry Pi B+: Eigene Beschriftung
  RFID-RC522-v2: A simple China made RFID-RC522 Reader; do check the pin labels, as this is a MFRC522 based clone.
